// Logisim project cpu.circ as structural Verilog: 1 circuit, main circuit cpu
module cpu (
  input  clk,
  input  [31:0] INSTRUCTION,
  input  [31:0] READ_DATA,
  output [31:0] WRITE_ADDRESS,
  output [31:0] PROGRAM_COUNTER,
  output [31:0] ra,
  output [31:0] sp,
  output [31:0] t0,
  output [31:0] t1,
  output [31:0] t2,
  output [31:0] s0,
  output [31:0] s1,
  output [31:0] a0,
  output [31:0] tohost,
  output [3:0] WRITE_ENABLE,
  output [31:0] WRITE_DATA
);

  wire ASel, BrEq, BrLt, BrUn, BSel, CSRSel, CSRWen, LB, LH, MemRW, PCSel, RegWEn, SB, SH;
  wire [1:0] WBSel;
  wire [2:0] func3, ImmSel;
  wire [3:0] ALUSel, multiplexer_7_out, multiplexer_8_out;
  wire [6:0] func7;
  wire [24:0] INSTRUCTION2;
  wire [31:0] adder_1_out, adder_2_out, bit_extender_1_out, bit_extender_2_out, imm32, multiplexer_1_out,
       multiplexer_2_out, multiplexer_3_out, multiplexer_4_out, multiplexer_5_out, multiplexer_10_out,
       PROGRAM_COUNTER2, r1, READ_DATA2, WB_data;

  Adder #(.width(32)) adder_1 (.a(PROGRAM_COUNTER), .b(32'h4), .out(adder_1_out));  // open: cin, cout
  Multiplexer #(.enable("false"), .width(32)) multiplexer_1 (
    .in0(adder_1_out), .in1(WRITE_ADDRESS), .out(multiplexer_1_out), .sel(PCSel));
  Register #(.width(32)) PC (.D(multiplexer_1_out), .clk(clk), .Q(PROGRAM_COUNTER));  // open: en, clr
  Register #(.width(32)) register_1 (
    .D(multiplexer_2_out), .clk(clk), .Q({func7, INSTRUCTION2[24:15], func3, INSTRUCTION2[11:0]}));  // open: en, clr
  Multiplexer #(.enable("false"), .width(32)) multiplexer_2 (
    .in0(INSTRUCTION), .in1(32'h13), .out(multiplexer_2_out), .sel(PCSel));
  Register #(.width(32)) register_2 (.D(PROGRAM_COUNTER), .clk(clk), .Q(PROGRAM_COUNTER2));  // open: en, clr
  // branch_comp branch_comp_1: pin names not known; wires that end beside it: r1, WRITE_DATA, BrUn, BrEq, BrLt
  // control_logic control_logic_1: pin names not known; wires that end beside it: {func7, INSTRUCTION2[24:15], func3, INSTRUCTION2[11:0]}, PCSel, RegWEn, ImmSel, BrEq, BrLt, BrUn, ASel, BSel, ALUSel, MemRW, WBSel, CSRSel, CSRWen, LB, LH, SB
  imm_gen imm_gen_1 (.inst({func7, INSTRUCTION2[24:15], func3, INSTRUCTION2[11:0]}), .ImmSel(ImmSel), .imm(imm32));
  // regfile regfile_1: pin names not known; wires that end beside it: INSTRUCTION2[19:15], INSTRUCTION2[24:20], INSTRUCTION2[11:7], WB_data, RegWEn, clk, ra, sp, t0, t1, t2, s0, s1, a0, r1, WRITE_DATA
  Multiplexer #(.enable("false"), .width(32)) multiplexer_3 (
    .in0(r1), .in1(PROGRAM_COUNTER2), .out(multiplexer_3_out), .sel(ASel));
  Multiplexer #(.enable("false"), .width(32)) multiplexer_4 (
    .in0(WRITE_DATA), .in1(imm32), .out(multiplexer_4_out), .sel(BSel));
  Multiplexer #(.enable("false"), .width(32)) multiplexer_5 (
    .in0(r1), .in1(imm32), .out(multiplexer_5_out), .sel(CSRSel));
  // alu alu_1: pin names not known; wires that end beside it: multiplexer_3_out, multiplexer_4_out, ALUSel, WRITE_ADDRESS
  Adder #(.width(32)) adder_2 (.a(PROGRAM_COUNTER2), .b(32'h4), .out(adder_2_out));  // open: cin, cout
  Multiplexer #(.enable("false"), .select(2), .width(32)) multiplexer_6 (
    .in0(READ_DATA2), .in1(WRITE_ADDRESS), .in2(adder_2_out), .in3(imm32), .out(WB_data), .sel(WBSel));
  Multiplexer #(.enable("false"), .width(4)) multiplexer_7 (
    .in0(4'b1111), .in1(4'b0011), .out(multiplexer_7_out), .sel(SH));
  csr csr_1 (.CSR_address(12'h51e), .CSR_din(multiplexer_5_out), .CSR_WE(CSRWen), .clk(clk), .tohost(tohost));
  Multiplexer #(.enable("false"), .width(4)) multiplexer_8 (
    .in0(multiplexer_7_out), .in1(4'b0001), .out(multiplexer_8_out), .sel(SB));
  Multiplexer #(.enable("false"), .width(4)) multiplexer_9 (
    .in0(4'b0000), .in1(multiplexer_8_out), .out(WRITE_ENABLE), .sel(MemRW));
  assign bit_extender_1_out = {{24{READ_DATA[7]}}, READ_DATA[7:0]};  // Bit_Extender bit_extender_1
  assign bit_extender_2_out = {{16{READ_DATA[15]}}, READ_DATA[15:0]};  // Bit_Extender bit_extender_2
  Multiplexer #(.enable("false"), .width(32)) multiplexer_10 (
    .in0(READ_DATA), .in1(bit_extender_2_out), .out(multiplexer_10_out), .sel(LH));
  Multiplexer #(.enable("false"), .width(32)) multiplexer_11 (
    .in0(multiplexer_10_out), .in1(bit_extender_1_out), .out(READ_DATA2), .sel(LB));

  // Other names for the same wires on the sheet: ALU_Output[31:0] = WRITE_ADDRESS; opcode[6:0] = INSTRUCTION2[6:0];
  //   rd[4:0] = INSTRUCTION2[11:7]; INSTRUCTION2 (some bits) = {func7, func3}; rs1[4:0] = INSTRUCTION2[19:15];
  //   rs2[4:0] = INSTRUCTION2[24:20]; r2[31:0] = WRITE_DATA

  // Notes on the sheet:
  //   Output to IMEM
  //   IMEM (do **NOT** move this)
  //   Inputs from IMEM
  //   Docode
  //   It is OK to move the PC, RegFile, ALU, MEM, Branch Comp, Imm Gen, and Control Logic to wherever is most convenient for you when constructing your CPU, and to delete this text
  //   Inputs/Outputs for testing. Do **NOT** move these.
  //   Outputs To DMEM
  //   DMEM (do **NOT** move this)
  //   Inputs From DMEM
endmodule
